# Fritzing sketch picus (saved by Fritzing 0.9.2b)
circuit board: 10cm x 2cm
breadboards: 1

parts:
  Q1 = Basic FET N-Channel [part_number=IRLZ34N package="TO220 [THT]"]
  U1 = ESP8266 WiFi Module [part_number=ESP8266]
  R1 = Resistor [tolerance=±5% resistance=33 package=THT]
  R2 = Resistor [tolerance=±5% resistance=10k package=THT]
  D1 = Rectifier Diode [part_number=1N4001 package="300 mil [THT]"]
  C1 = Electrolytic Capacitor [capacitance=470µF voltage=35V package="200 mil [THT, electrolytic]"]
  VCC1 = Battery
  L1 = Solenoid
  R3 = Resistor [tolerance=±5% resistance=10k package=THT]
  DC/DC = DC/DC Module - MT3608

nets:
  N1: Q1.gate, R2.Pin_0
  N2: Q1.drain, D1.anode, L1.pin2
  N3: Q1.source, U1.GND, C1.-, VCC1.-, DC/DC.VOUT-, DC/DC.VIN-
  N4: U1.VCC, U1.CH_PD, VCC1.+, R3.Pin_1, DC/DC.VIN+
  N5: U1.RST, R3.Pin_0
  N6: U1.GPIO_2, R2.Pin_1
  N7: R1.Pin_0, DC/DC.VOUT+
  N8: R1.Pin_1, D1.cathode, C1.+, L1.pin1

custom parts:
  ESP8266 WiFi Module: Generic WiFi Module based on the ESP8266 with onboard PCB antenna and UART communications
  DC/DC Module - MT3608: Description: Breakout for the MT3608
