# Fritzing sketch programming (saved by Fritzing 0.9.2b)
breadboards: 1

parts:
  U1 = ESP8266 WiFi Module [part_number=ESP8266]
  Bauteil1 = FTDI Basic Programmer

nets:
  N1: U1.RXD, Bauteil1.TXO
  N2: U1.VCC, U1.CH_PD, Bauteil1.POWER
  GND: U1.GPIO_0, U1.GND, Bauteil1.GND
  N3: U1.TXD, Bauteil1.RXI

custom parts:
  ESP8266 WiFi Module: Generic WiFi Module based on the ESP8266 with onboard PCB antenna and UART communications
